// Logisim project SISTEMAS.circ as structural Verilog: 1 circuit, main circuit main
module main (
  input  A,
  input  B,
  input  C,
  output D,
  output E,
  output F,
  output G,
  output H,
  output I,
  output J,
  output K,
  output L,
  output M,
  output N,
  output O,
  output P,
  output Q,
  output R,
  output S,
  output T,
  output U,
  output V,
  output W,
  output X
);

  wire and_1_out, and_9_out, and_10_out, and_11_out, and_12_out, and_13_out, and_14_out, and_16_out,
       and_17_out, and_18_out, and_19_out, and_20_out, and_21_out, and_22_out, and_23_out, and_27_out,
       and_28_out, nor_1_out, nor_2_out, not_1_out, not_2_out, not_3_out, or_1_out, or_2_out, xor_1_out;

  not not_1 (not_1_out, A);
  not not_2 (not_2_out, B);
  not not_3 (not_3_out, C);
  or or_1 (or_1_out, C, B);
  xor xor_1 (xor_1_out, C, B);
  nor nor_1 (nor_1_out, B, C);
  and and_1 (and_1_out, C, B);
  nor nor_2 (nor_2_out, B, C);
  or or_2 (or_2_out, not_3_out, B);
  and and_2 (D, not_2_out, not_1_out);
  and and_3 (E, not_1_out, A);
  and and_4 (F, B, A);
  and and_5 (G, not_1_out, not_1_out);
  and and_6 (H, not_1_out, B);
  and and_7 (I, not_1_out, B);
  and and_8 (J, not_2_out, not_1_out);
  and and_9 (and_9_out, not_1_out, or_1_out);
  and and_10 (and_10_out, xor_1_out, A);
  and and_11 (and_11_out, not_1_out, nor_1_out);
  and and_12 (and_12_out, and_1_out, A);
  and and_13 (and_13_out, not_1_out, B);
  and and_14 (and_14_out, or_1_out, A);
  and and_15 (N, not_1_out, not_1_out);
  and and_16 (and_16_out, not_1_out, C);
  and and_17 (and_17_out, xor_1_out, A);
  and and_18 (and_18_out, or_1_out, not_1_out);
  and and_19 (and_19_out, xor_1_out, A);
  and and_20 (and_20_out, and_1_out, not_1_out);
  and and_21 (and_21_out, or_1_out, A);
  and and_22 (and_22_out, or_1_out, not_1_out);
  and and_23 (and_23_out, not_1_out, nor_2_out);
  and and_24 (T, not_1_out, B);
  and and_25 (U, not_1_out, not_1_out);
  and and_26 (V, not_3_out, not_3_out);
  and and_27 (and_27_out, not_1_out, or_2_out);
  and and_28 (and_28_out, not_1_out, not_2_out);
  or or_3 (K, and_9_out, and_10_out);
  or or_4 (L, and_11_out, and_12_out);
  or or_5 (M, and_13_out, and_14_out);
  or or_6 (O, and_16_out, and_17_out);
  or or_7 (P, and_18_out, and_19_out);
  or or_8 (Q, and_20_out, and_21_out);
  or or_9 (R, and_22_out, not_1_out);
  or or_10 (S, and_23_out, A);
  or or_11 (W, and_27_out, not_1_out);
  or or_12 (X, and_28_out, C);
endmodule
